// Digital circuit UTS_1_1.dig as structural Verilog
module UTS_1_1 (
  input  A,
  input  B,
  input  C,
  output X
);

  wire and_1_out, and_2_out, and_3_out, and_4_out, and_5_out, not_1_out, or_1_out, or_2_out;

  and and_1 (and_1_out, A, C);
  and and_2 (and_2_out, A, B);
  and and_3 (and_3_out, B, C);
  or or_1 (or_1_out, A, B, C);
  or or_2 (or_2_out, and_2_out, and_3_out, and_1_out);
  not not_1 (not_1_out, or_2_out);
  and and_4 (and_4_out, A, B, C);
  and and_5 (and_5_out, or_1_out, not_1_out);
  or or_3 (X, and_5_out, and_4_out);

  // Notes on the sheet:
  //   UTS RANGKAIAN DIGITAL
  //   UJIAN TENGAH SEMESTER
  //   (AB + AC + BC) ' (A + B + C) + ABC
  //   | ABDUL WAHAB
endmodule
