// Digital circuit UTS_1_11.dig as structural Verilog
module UTS_1_11 (
  input  X,
  input  Y,
  input  Z,
  output H
);

  wire and_1_out, and_2_out, and_3_out, and_4_out;

  and and_1 (and_1_out, ~X, ~Y, Z);  // And
  and and_2 (and_2_out, X, Y, ~Z);  // And
  and and_3 (and_3_out, ~X, Y, Z);  // And
  and and_4 (and_4_out, X, Y);
  or or_1 (H, and_2_out, and_4_out, and_1_out, and_3_out);

  // Notes on the sheet:
  //   UTS RANGKAIAN DIGITAL
  //   UJIAN TENGAH SEMESTER
  //   X'Y'Z + XYZ' + X'YZ + XY
  //   | ABDUL WAHAB
endmodule
