// Digital circuit UTS_1_15.dig as structural Verilog
module UTS_1_15 (
  input  A,
  input  B,
  input  C,
  input  D,
  output X
);

  wire and_1_out, and_2_out, and_3_out, and_4_out;

  and and_1 (and_1_out, A, B, ~C);  // And
  and and_2 (and_2_out, ~C, D);  // And
  and and_3 (and_3_out, ~B, C, ~D);  // And
  and and_4 (and_4_out, ~A, C, ~D);  // And
  or or_1 (X, and_3_out, and_1_out, and_4_out, and_2_out);

  // Notes on the sheet:
  //   UTS RANGKAIAN DIGITAL
  //   UJIAN TENGAH SEMESTER
  //   | ABDUL WAHAB
  //   ABC' + C'D + A'CD' + B'CD'
endmodule
