// Digital circuit UTS_1_2.dig as structural Verilog
module UTS_1_2 (
  input  A,
  input  B,
  input  C,
  input  D,
  output X
);

  wire and_1_out, and_2_out, and_3_out, and_4_out, and_5_out, and_6_out, not_1_out, not_2_out, not_3_out,
       not_4_out, not_5_out, not_6_out, not_7_out, not_8_out;

  not not_1 (not_1_out, B);
  not not_2 (not_2_out, A);
  not not_3 (not_3_out, C);
  not not_4 (not_4_out, A);
  not not_5 (not_5_out, A);
  and and_1 (and_1_out, not_2_out, not_1_out, not_3_out);
  not not_6 (not_6_out, C);
  and and_2 (and_2_out, not_4_out, C, D);
  and and_3 (and_3_out, not_5_out, B, D);
  not not_7 (not_7_out, A);
  not not_8 (not_8_out, D);
  and and_4 (and_4_out, not_7_out, not_6_out, not_8_out);
  and and_5 (and_5_out, A, B, C);
  and and_6 (and_6_out, A, B, C);
  or or_1 (X, and_3_out, and_1_out, and_6_out, and_5_out, and_4_out, and_2_out);

  // Notes on the sheet:
  //   UTS RANGKAIAN DIGITAL
  //   UJIAN TENGAH SEMESTER
  //   A'B'C' + A'CD + A'C'D' + A'BD + ABC + AB'C
  //   | ABDUL WAHAB
endmodule
