// Digital circuit UTS_1_3.dig as structural Verilog
module UTS_1_3 (
  input  X,
  input  Y,
  input  Z,
  output X_2
);

  wire and_1_out, and_2_out, and_3_out, not_1_out, not_2_out, not_3_out, not_4_out;

  not not_1 (not_1_out, Y);
  not not_2 (not_2_out, X);
  not not_3 (not_3_out, Z);
  not not_4 (not_4_out, Z);
  and and_1 (and_1_out, X, Y);
  and and_2 (and_2_out, not_2_out, not_1_out, not_3_out);
  and and_3 (and_3_out, Y, not_4_out);
  or or_1 (X_2, and_1_out, and_2_out, and_3_out);

  // Notes on the sheet:
  //   UTS RANGKAIAN DIGITAL
  //   UJIAN TENGAH SEMESTER
  //   X'Y'Z' + YZ' + XY
  //   | ABDUL WAHAB
endmodule
