// Digital circuit UTS_1_4.dig as structural Verilog
module UTS_1_4 (
  input  A,
  input  B,
  input  C,
  input  D,
  output X
);

  wire and_1_out, and_2_out, and_3_out, not_1_out, not_2_out, not_3_out;

  not not_1 (not_1_out, A);
  and and_1 (and_1_out, not_1_out, B);
  not not_2 (not_2_out, B);
  not not_3 (not_3_out, A);
  and and_2 (and_2_out, C, D);
  and and_3 (and_3_out, not_3_out, not_2_out, C);
  or or_1 (X, and_1_out, and_3_out, and_2_out);

  // Notes on the sheet:
  //   UTS RANGKAIAN DIGITAL
  //   UJIAN TENGAH SEMESTER
  //   | ABDUL WAHAB
  //   A'B + A'B'C + CD
endmodule
