// Digital circuit UTS_1_5.dig as structural Verilog
module UTS_1_5 (
  input  A,
  input  B,
  input  C,
  input  D,
  output X
);

  wire and_1_out, and_2_out, and_3_out, and_4_out, not_1_out, not_2_out, not_3_out, not_4_out, not_5_out,
       not_6_out;

  not not_1 (not_1_out, B);
  not not_2 (not_2_out, A);
  and and_1 (and_1_out, not_3_out, not_1_out, not_4_out);
  not not_3 (not_3_out, A);
  not not_4 (not_4_out, D);
  and and_2 (and_2_out, not_2_out, D);
  not not_5 (not_5_out, C);
  not not_6 (not_6_out, D);
  and and_3 (and_3_out, B, C, D);
  and and_4 (and_4_out, B, not_5_out, not_6_out);
  or or_1 (X, and_4_out, and_1_out, and_3_out, and_2_out);

  // Notes on the sheet:
  //   UTS RANGKAIAN DIGITAL
  //   UJIAN TENGAH SEMESTER
  //   A'B'D' + A'D + BCD + BC'D'
  //   | ABDUL WAHAB
endmodule
