// Digital circuit UTS_1_8.dig as structural Verilog
module UTS_1_8 (
  input  A,
  input  B,
  input  C,
  input  D,
  output X
);

  wire and_1_out, and_2_out, and_3_out, and_4_out, and_5_out;

  and and_1 (and_1_out, ~A, B, ~D);  // And
  and and_2 (and_2_out, B, C, D);
  and and_3 (and_3_out, B, D);
  and and_4 (and_4_out, A, B, ~C);  // And
  and and_5 (and_5_out, A, C, B);
  or or_1 (X, and_1_out, and_4_out, and_2_out, and_5_out, and_3_out);

  // Notes on the sheet:
  //   UTS RANGKAIAN DIGITAL
  //   UJIAN TENGAH SEMESTER
  //   A'BD' +BDC + ABC' + BD + ABC
  //   | ABDUL WAHAB
endmodule
