// Digital circuit UTS_1_9.dig as structural Verilog
module UTS_1_9 (
  input  A,
  input  B,
  input  C,
  input  D,
  output X
);

  wire and_1_out, and_2_out, and_3_out, and_4_out, and_5_out;

  and and_1 (and_1_out, A, ~B, ~C);  // And
  and and_2 (and_2_out, A, ~C, ~D);  // And
  and and_3 (and_3_out, A, B, D);
  and and_4 (and_4_out, B, ~C, D);  // And
  and and_5 (and_5_out, ~A, B, ~C, ~D);  // And
  or or_1 (X, and_1_out, and_5_out, and_3_out, and_4_out, and_2_out);

  // Notes on the sheet:
  //   UTS RANGKAIAN DIGITAL
  //   UJIAN TENGAH SEMESTER
  //   AB'C' + AC'D' + ABD + BC'D + A'BC'D'
  //   | ABDUL WAHAB
endmodule
